// Logisim project ALU_comp.circ as structural Verilog: 1 circuit, main circuit ALU
module ALU (
  input  [31:0] input1,
  input  [31:0] input2,
  input  [3:0] ALUControl,
  output [31:0] ALUResult,
  output Zero,
  output LessThan
);

  wire comparator_1_eq, comparator_1_lt;
  wire [31:0] adder_1_out, adder_2_out, and_1_out, and_2_out, multiplexer_1_out, multiplexer_2_out,
       not_1_out, or_1_out, shifter_1_out, shifter_2_out, shifter_3_out, shifter_4_out, xor_1_out;

  ROM #(.addrWidth(20), .dataWidth(16)) rom_1 ();  // open: addr, data
  assign not_1_out = ~input2;  // NOT_Gate not_1, 32 bits wide
  Adder #(.width(32)) adder_1 (.a(input1), .b(input2), .out(adder_1_out));  // open: cin, cout
  Adder #(.width(32)) adder_2 (.a(input1), .b(not_1_out), .out(adder_2_out), .cin(1'b1));  // open: cout
  Comparator #(.width(32)) comparator_1 (
    .a(input1), .b(input2), .eq(comparator_1_eq), .lt(comparator_1_lt));  // open: gt
  Shifter #(.width(32)) shifter_1 (.in(input1), .\dist (input2[4:0]), .out(shifter_1_out));
  Shifter #(.shift("lr"), .width(32)) shifter_2 (.in(input1), .\dist (input2[4:0]), .out(shifter_2_out));
  Shifter #(.shift("ar"), .width(32)) shifter_3 (.in(input1), .\dist (input2[4:0]), .out(shifter_3_out));
  Shifter #(.shift("rr"), .width(32)) shifter_4 (.in(input1), .\dist (input2[4:0]), .out(shifter_4_out));
  assign and_1_out = input1 & input2;  // AND_Gate and_1, 32 bits wide
  assign and_2_out = input1 & ~input2;  // AND_Gate and_2, 32 bits wide
  assign or_1_out = input1 | input2;  // OR_Gate or_1, 32 bits wide
  assign xor_1_out = input1 ^ input2;  // XOR_Gate xor_1, 32 bits wide
  Multiplexer #(.width(32)) multiplexer_1 (
    .in0({32{1'b0}}), .in1(32'h1), .out(multiplexer_1_out), .sel(comparator_1_eq));
  Multiplexer #(.width(32)) multiplexer_2 (
    .in0({32{1'b0}}), .in1(32'h1), .out(multiplexer_2_out), .sel(comparator_1_lt));
  Multiplexer #(.select(4), .width(32)) multiplexer_3 (
    .in0(and_1_out), .in1(and_2_out), .in2(or_1_out), .in3(xor_1_out), .in4(adder_1_out), .in5(adder_2_out),
    .in6(multiplexer_1_out), .in7(multiplexer_2_out), .in8(shifter_1_out), .in9(shifter_2_out),
    .in10(shifter_3_out), .in11(shifter_4_out), .out(ALUResult), .sel(ALUControl));  // open: in12, in13, in14, in15
  orReduce orreduce_1 (.stringIn(multiplexer_1_out), .orReduce(Zero));
  orReduce orreduce_2 (.stringIn(multiplexer_2_out), .orReduce(LessThan));
endmodule
