// Logisim project ITypeChecker.circ as structural Verilog: 1 circuit, main circuit isIType
module isIType (
  input  [4:0] OpCode,
  output IType
);

  wire and_1_out, and_2_out, comparator_1_gt, comparator_2_lt, comparator_3_gt, comparator_4_lt;

  Comparator #(.mode("unsigned"), .width(5)) comparator_1 (
    .a(OpCode), .b(5'b00011), .gt(comparator_1_gt));  // open: eq, lt
  Comparator #(.mode("unsigned"), .width(5)) comparator_2 (
    .a(OpCode), .b(5'b01100), .lt(comparator_2_lt));  // open: gt, eq
  Comparator #(.mode("unsigned"), .width(5)) comparator_3 (
    .a(OpCode), .b(5'b01111), .gt(comparator_3_gt));  // open: eq, lt
  Comparator #(.mode("unsigned"), .width(5)) comparator_4 (
    .a(OpCode), .b(5'b11100), .lt(comparator_4_lt));  // open: gt, eq
  and and_1 (and_1_out, comparator_1_gt, comparator_2_lt);
  and and_2 (and_2_out, comparator_3_gt, comparator_4_lt);
  or or_1 (IType, and_1_out, and_2_out);
endmodule
