// Logisim project RegisterFile.circ as structural Verilog: 1 circuit, main circuit registerFile
module registerFile (
  input  [31:0] WriteData,
  input  clk,
  input  [2:0] readReg1,
  input  WriteEnable,
  input  [2:0] readReg2,
  input  [2:0] WriteRegister,
  output [31:0] reg1,
  output [31:0] readData1,
  output [31:0] reg2,
  output [31:0] reg3,
  output [31:0] readData2,
  output [31:0] reg4,
  output [31:0] reg5,
  output [31:0] reg6,
  output [31:0] reg7
);

  wire decoder_1_out1, decoder_1_out2, decoder_1_out3, decoder_1_out4, decoder_1_out5, decoder_1_out6,
       decoder_1_out7;

  Decoder #(.select(3)) decoder_1 (
    .out1(decoder_1_out1), .out2(decoder_1_out2), .out3(decoder_1_out3), .out4(decoder_1_out4),
    .out5(decoder_1_out5), .out6(decoder_1_out6), .out7(decoder_1_out7), .sel(WriteRegister), .en(WriteEnable));  // open: out0
  Register #(.width(32)) register_1 (.D(WriteData), .en(decoder_1_out1), .clk(clk), .Q(reg1));  // open: clr
  Register #(.width(32)) register_2 (.D(WriteData), .en(decoder_1_out2), .clk(clk), .Q(reg2));  // open: clr
  Register #(.width(32)) register_3 (.D(WriteData), .en(decoder_1_out3), .clk(clk), .Q(reg3));  // open: clr
  Register #(.width(32)) register_4 (.D(WriteData), .en(decoder_1_out4), .clk(clk), .Q(reg4));  // open: clr
  Register #(.width(32)) register_5 (.D(WriteData), .en(decoder_1_out5), .clk(clk), .Q(reg5));  // open: clr
  Register #(.width(32)) register_6 (.D(WriteData), .en(decoder_1_out6), .clk(clk), .Q(reg6));  // open: clr
  Register #(.width(32)) register_7 (.D(WriteData), .en(decoder_1_out7), .clk(clk), .Q(reg7));  // open: clr
  Multiplexer #(.select(3), .width(32)) multiplexer_1 (
    .in0({32{1'b0}}), .in1(reg1), .in2(reg2), .in3(reg3), .in4(reg4), .in5(reg5), .in6(reg6), .in7(reg7),
    .out(readData1), .sel(readReg1));
  Multiplexer #(.select(3), .width(32)) multiplexer_2 (
    .in0({32{1'b0}}), .in1(reg1), .in2(reg2), .in3(reg3), .in4(reg4), .in5(reg5), .in6(reg6), .in7(reg7),
    .out(readData2), .sel(readReg2));
endmodule
