// Logisim project Single_Cycle.circ as structural Verilog: 1 circuit, main circuit DataPath
module DataPath (
);

  wire alu_1_lessthan, alu_1_zero, applyBranch, clock_1_out, hazardcontrol_1_insertnop, immlogic_1_applyimm,
       jumpImmediate, jumpRegister, maincontrol_1_alusrc, maincontrol_1_eqbranch, maincontrol_1_forcer7,
       maincontrol_1_gebranch, maincontrol_1_ltbranch, maincontrol_1_memwrite, maincontrol_1_noteqbranch,
       maincontrol_1_regdst, maincontrol_1_regwrite, maincontrol_1_writeaddress, maincontrol_1_writebus,
       undriven;
  wire [1:0] instructionsplitter_1_func;
  wire [2:0] instructionsplitter_1_rega, instructionsplitter_1_regb, instructionsplitter_1_regd,
       multiplexer_2_out, multiplexer_3_out;
  wire [3:0] alucontrol_1_aluselect, maincontrol_1_aluop;
  wire [4:0] instructionsplitter_1_imm5, instructionsplitter_1_opcode;
  wire [10:0] immlogic_1_imm11, instructionsplitter_1_imm11;
  wire [15:0] multiplexer_1_out, register_2_q, rom_1_data;
  wire [19:0] adder_1_out, pcbox_1_nextpc, register_1_q;
  wire [31:0] alu_1_aluresult, bit_extender_1_out, bit_extender_2_out, bit_extender_3_out, multiplexer_4_out,
       multiplexer_5_out, multiplexer_6_out, multiplexer_7_out, ram_1_dout, registerfile_1_readdata1,
       registerfile_1_readdata2, registerfile_1_reg1, registerfile_1_reg2, registerfile_1_reg3,
       registerfile_1_reg4, registerfile_1_reg5, registerfile_1_reg6, registerfile_1_reg7;

  Clock clock_1 (.out(clock_1_out));
  Register #(.width(20)) register_1 (
    .D(pcbox_1_nextpc), .en(1'b1), .clk(clock_1_out), .Q(register_1_q), .clr(undriven));
  ROM #(.addrWidth(20), .dataWidth(16)) rom_1 (.addr(register_1_q), .data(rom_1_data));
  Adder #(.width(20)) adder_1 (.a(20'h1), .b(register_1_q), .out(adder_1_out));  // open: cin, cout
  Multiplexer #(.width(16)) multiplexer_1 (
    .in0(rom_1_data), .in1({16{1'b0}}), .out(multiplexer_1_out), .sel(hazardcontrol_1_insertnop));
  HazardControl hazardcontrol_1 (
    .applyBranch(applyBranch), .jumpImmediate(jumpImmediate), .jumpRegister(jumpRegister),
    .insertNop(hazardcontrol_1_insertnop));
  Register #(.width(16)) register_2 (
    .D(multiplexer_1_out), .en(1'b1), .clk(clock_1_out), .Q(register_2_q));  // open: clr
  instructionSplitter instructionsplitter_1 (
    .instruction(register_2_q), .func(instructionsplitter_1_func), .RegD(instructionsplitter_1_regd),
    .Imm5(instructionsplitter_1_imm5), .RegB(instructionsplitter_1_regb), .RegA(instructionsplitter_1_rega),
    .Imm11(instructionsplitter_1_imm11), .Opcode(instructionsplitter_1_opcode));
  MainControl maincontrol_1 (
    .OpCode(instructionsplitter_1_opcode), .EqBranch(maincontrol_1_eqbranch),
    .GeBranch(maincontrol_1_gebranch), .NotEqBranch(maincontrol_1_noteqbranch),
    .LtBranch(maincontrol_1_ltbranch), .RegDst(maincontrol_1_regdst), .ForceR7(maincontrol_1_forcer7),
    .WriteBus(maincontrol_1_writebus), .WriteAddress(maincontrol_1_writeaddress),
    .MemWrite(maincontrol_1_memwrite), .ALUSrc(maincontrol_1_alusrc), .RegWrite(maincontrol_1_regwrite),
    .JumpImm(jumpImmediate), .JumpReg(jumpRegister), .ALUOp(maincontrol_1_aluop));  // open: MemRead
  ImmLogic immlogic_1 (
    .OpCode(instructionsplitter_1_opcode), .nextInstruction(multiplexer_1_out),
    .ApplyImm(immlogic_1_applyimm), .Imm11(immlogic_1_imm11));
  Multiplexer #(.width(3)) multiplexer_2 (
    .in0(instructionsplitter_1_regd), .in1(instructionsplitter_1_regb), .out(multiplexer_2_out),
    .sel(maincontrol_1_regdst));
  // Probe on registerfile_1_reg1
  Multiplexer #(.width(3)) multiplexer_3 (
    .in0(multiplexer_2_out), .in1(3'b111), .out(multiplexer_3_out), .sel(maincontrol_1_forcer7));
  // Probe on registerfile_1_reg2
  assign bit_extender_1_out = {{27{instructionsplitter_1_imm5[4]}}, instructionsplitter_1_imm5};  // Bit_Extender bit_extender_1
  assign bit_extender_2_out = {{16{immlogic_1_imm11[10]}}, {immlogic_1_imm11, instructionsplitter_1_imm5}};  // Bit_Extender bit_extender_2
  // Probe on registerfile_1_reg3
  registerFile registerfile_1 (
    .WriteEnable(maincontrol_1_regwrite), .WriteRegister(multiplexer_3_out), .clk(clock_1_out),
    .WriteData(multiplexer_7_out), .readReg2(instructionsplitter_1_regb),
    .readReg1(instructionsplitter_1_rega), .reg2(registerfile_1_reg2), .reg3(registerfile_1_reg3),
    .reg4(registerfile_1_reg4), .reg7(registerfile_1_reg7), .reg5(registerfile_1_reg5),
    .reg6(registerfile_1_reg6), .reg1(registerfile_1_reg1), .readData1(registerfile_1_readdata1),
    .readData2(registerfile_1_readdata2));
  Multiplexer #(.width(32)) multiplexer_4 (
    .in0(bit_extender_1_out), .in1(bit_extender_2_out), .out(multiplexer_4_out), .sel(immlogic_1_applyimm));
  ALUControl alucontrol_1 (
    .ALUOp(maincontrol_1_aluop), .FuncCode(instructionsplitter_1_func), .ALUSelect(alucontrol_1_aluselect));
  // Probe on registerfile_1_reg4
  Multiplexer #(.width(32)) multiplexer_5 (
    .in0(registerfile_1_readdata2), .in1(multiplexer_4_out), .out(multiplexer_5_out),
    .sel(maincontrol_1_alusrc));
  // Probe on registerfile_1_reg5
  branchControl branchcontrol_1 (
    .geBranch(maincontrol_1_gebranch), .lessThan(alu_1_lessthan), .zero(alu_1_zero),
    .LtBranch(maincontrol_1_ltbranch), .notEqBranch(maincontrol_1_noteqbranch),
    .EqBranch(maincontrol_1_eqbranch), .applyBranch(applyBranch));
  // Probe on registerfile_1_reg6
  ALU alu_1 (
    .input1(registerfile_1_readdata1), .input2(multiplexer_5_out), .ALUControl(alucontrol_1_aluselect),
    .ALUResult(alu_1_aluresult), .Zero(alu_1_zero), .LessThan(alu_1_lessthan));
  // Probe on registerfile_1_reg7
  RAM #(.addrWidth(20), .dataWidth(32), .enables("line")) ram_1 (
    .addr(alu_1_aluresult[19:0]), .we(maincontrol_1_memwrite), .clk(clock_1_out),
    .din(registerfile_1_readdata2), .dout(ram_1_dout));
  PCBox pcbox_1 (
    .PC(register_1_q), .Imm11(instructionsplitter_1_imm11), .Imm5(instructionsplitter_1_imm5),
    .applyBranch(applyBranch), .jumpImmediate(jumpImmediate), .jumpReg(jumpRegister),
    .regValue(registerfile_1_readdata1), .OpCode(instructionsplitter_1_opcode),
    .nextIntruction(multiplexer_1_out), .nextPC(pcbox_1_nextpc));
  Multiplexer #(.width(32)) multiplexer_6 (
    .in0(alu_1_aluresult), .in1(ram_1_dout), .out(multiplexer_6_out), .sel(maincontrol_1_writebus));
  assign bit_extender_3_out = {{12{adder_1_out[19]}}, adder_1_out};  // Bit_Extender bit_extender_3
  Multiplexer #(.width(32)) multiplexer_7 (
    .in0(multiplexer_6_out), .in1(bit_extender_3_out), .out(multiplexer_7_out),
    .sel(maincontrol_1_writeaddress));

  // Notes on the sheet:
  //   contents of rom_1 (hex, n*v repeats v):
  //   3040 f001 302f aa20 302d aa21 3028 aa22 3029 aa23 303e aa24 3037 aa25 302a aa26 302d aa27 3020 aa28
  //   303f aa29 4021 306a 996c 950 8288 a4bf a4c0 9ea5 aca0 acdf 449f e7f9 4121 e7f5 e000
  //   R1
  //   R2
  //   R3
  //   R4
  //   R5
  //   R6
  //   R7
endmodule
