// Logisim project hazardCircuit.circ as structural Verilog: 1 circuit, main circuit HazardControl
module HazardControl (
  input  applyBranch,
  input  jumpImmediate,
  input  jumpRegister,
  output insertNop
);

  or or_1 (insertNop, applyBranch, jumpImmediate, jumpRegister);
endmodule
