// Logisim project ALUControls.circ as structural Verilog: 1 circuit, main circuit ALUControl
module ALUControl (
  input  [3:0] ALUOp,
  input  [1:0] FuncCode,
  output [3:0] ALUSelect
);

  wire [3:0] multiplexer_1_out, multiplexer_2_out;

  Multiplexer #(.select(2), .width(4)) multiplexer_1 (
    .in0(4'b0000), .in1(4'b0001), .in2(4'b0010), .in3(4'b0011), .out(multiplexer_1_out), .sel(FuncCode));
  Multiplexer #(.select(2), .width(4)) multiplexer_2 (
    .in0(4'b0100), .in1(4'b0101), .in2(4'b0110), .in3(4'b0111), .out(multiplexer_2_out), .sel(FuncCode));
  Multiplexer #(.select(4), .width(4)) multiplexer_3 (
    .in0(ALUOp), .in1(ALUOp), .in2(ALUOp), .in3(ALUOp), .in4(ALUOp), .in5(ALUOp), .in6(ALUOp), .in7(ALUOp),
    .in8(ALUOp), .in9(ALUOp), .in10(ALUOp), .in11(ALUOp), .in14(multiplexer_1_out), .in15(multiplexer_2_out),
    .out(ALUSelect), .sel(ALUOp));  // open: in12, in13
endmodule
