// Logisim project ImmCircuit.circ as structural Verilog: 1 circuit, main circuit ImmLogic
module ImmLogic (
  input  [4:0] OpCode,
  input  [15:0] nextInstruction,
  output ApplyImm,
  output [10:0] Imm11
);

  wire comparator_1_eq, isitype_1_itype;
  wire [4:0] instructionsplitter_1_opcode;

  isIType isitype_1 (.OpCode(OpCode), .IType(isitype_1_itype));
  instructionSplitter instructionsplitter_1 (
    .instruction(nextInstruction), .Imm11(Imm11), .Opcode(instructionsplitter_1_opcode));  // open: func, RegD, Imm5, RegB, RegA
  Comparator #(.width(5)) comparator_1 (
    .a(instructionsplitter_1_opcode), .b(5'b11110), .eq(comparator_1_eq));  // open: gt, lt
  and and_1 (ApplyImm, isitype_1_itype, comparator_1_eq);
endmodule
