// Logisim project InstructionSplit.circ as structural Verilog: 1 circuit, main circuit instructionSplitter
module instructionSplitter (
  input  [15:0] instruction,
  output [1:0] func,
  output [2:0] RegD,
  output [4:0] Imm5,
  output [2:0] RegB,
  output [2:0] RegA,
  output [10:0] Imm11,
  output [4:0] Opcode
);


  assign func = instruction[1:0];
  assign Imm5 = instruction[4:0];
  assign Imm11 = instruction[10:0];
  assign Opcode = instruction[15:11];
  assign RegA = instruction[10:8];
  assign RegB = instruction[7:5];
  assign RegD = instruction[4:2];
endmodule
