// Logisim project MainControls.circ as structural Verilog: 1 circuit, main circuit MainControl
module MainControl (
  input  [4:0] OpCode,
  output EqBranch,
  output GeBranch,
  output NotEqBranch,
  output LtBranch,
  output RegDst,
  output ForceR7,
  output MemRead,
  output WriteBus,
  output WriteAddress,
  output MemWrite,
  output ALUSrc,
  output RegWrite,
  output JumpImm,
  output JumpReg,
  output [3:0] ALUOp
);

  wire decoder_1_out0, decoder_1_out1, decoder_1_out4, decoder_1_out5, decoder_1_out6, decoder_1_out7,
       decoder_1_out8, decoder_1_out9, decoder_1_out10, decoder_1_out11, decoder_1_out12, decoder_1_out13,
       decoder_1_out14, decoder_1_out15, decoder_1_out28, decoder_1_out30, decoder_1_out31;

  Decoder #(.enable("false"), .select(5)) decoder_1 (
    .out0(decoder_1_out0), .out1(decoder_1_out1), .out4(decoder_1_out4), .out5(decoder_1_out5),
    .out6(decoder_1_out6), .out7(decoder_1_out7), .out8(decoder_1_out8), .out9(decoder_1_out9),
    .out10(decoder_1_out10), .out11(decoder_1_out11), .out12(decoder_1_out12), .out13(decoder_1_out13),
    .out14(decoder_1_out14), .out15(decoder_1_out15), .out16(EqBranch), .out17(NotEqBranch),
    .out18(LtBranch), .out19(GeBranch), .out20(MemRead), .out21(MemWrite), .out27(JumpReg),
    .out28(decoder_1_out28), .out29(ForceR7), .out30(decoder_1_out30), .out31(decoder_1_out31), .sel(OpCode));  // open: out2, out3, out22, out23, out24, out25, out26
  or or_1 (ALUOp[3], decoder_1_out0, decoder_1_out1, decoder_1_out12, decoder_1_out13, decoder_1_out14, decoder_1_out15);
  nor nor_1 (ALUOp[2], decoder_1_out4, decoder_1_out5, decoder_1_out6, decoder_1_out7, decoder_1_out12, decoder_1_out13, decoder_1_out14, decoder_1_out15);
  or or_2 (ALUOp[1], decoder_1_out0, decoder_1_out1, decoder_1_out6, decoder_1_out7, decoder_1_out10, decoder_1_out11, decoder_1_out14, decoder_1_out15);
  nor nor_2 (ALUOp[0], decoder_1_out0, decoder_1_out4, decoder_1_out6, decoder_1_out8, decoder_1_out10, decoder_1_out12, decoder_1_out14, MemRead, MemWrite);
  nor nor_3 (RegDst, decoder_1_out0, decoder_1_out1);
  or or_3 (WriteAddress, JumpReg, ForceR7);
  nor nor_4 (ALUSrc, decoder_1_out0, decoder_1_out1, EqBranch, NotEqBranch, LtBranch, GeBranch);
  nor nor_5 (RegWrite, EqBranch, NotEqBranch, LtBranch, GeBranch, MemWrite, decoder_1_out28, decoder_1_out30, decoder_1_out31);
  or or_4 (JumpImm, decoder_1_out28, ForceR7);

  assign WriteBus = MemRead;

  // Notes on the sheet:
  //   3
endmodule
