// Logisim project branchCircuit.circ as structural Verilog: 1 circuit, main circuit branchControl
module branchControl (
  input  geBranch,
  input  lessThan,
  input  zero,
  input  LtBranch,
  input  notEqBranch,
  input  EqBranch,
  output applyBranch
);

  wire and_1_out, and_2_out, and_3_out, and_4_out;

  and and_1 (and_1_out, geBranch, ~lessThan);  // AND_Gate
  or or_1 (applyBranch, and_1_out, and_2_out, and_3_out, and_4_out);
  and and_2 (and_2_out, LtBranch, lessThan);
  and and_3 (and_3_out, notEqBranch, ~zero);  // AND_Gate
  and and_4 (and_4_out, EqBranch, zero);
endmodule
