// Logisim project forwardBox.circ as structural Verilog: 4 circuits, main circuit forwardControl
module forwardControl (
  input  [2:0] Rd_Ex,
  input  RegWrite_Ex,
  input  [2:0] Inst_Ra,
  input  RegWrite_Mem,
  input  [2:0] Rd_Mem,
  input  RegWrite_Wb,
  input  [2:0] Rd_Wb,
  input  [2:0] Inst_Rb,
  output [1:0] ForwardA,
  output [1:0] ForwardB
);

  wire ex_sense_1_ex_hazard, ex_sense_2_ex_hazard, mem_sense_1_mem_hazard, mem_sense_2_mem_hazard,
       wb_sense_1_wb_hazard, wb_sense_2_wb_hazard;

  EX_SENSE ex_sense_1 (.Rd_Ex(Rd_Ex), .RegWrite_Ex(RegWrite_Ex), .Inst_Rx(Inst_Ra), .EX_HAZARD(ex_sense_1_ex_hazard));
  MEM_SENSE mem_sense_1 (
    .RegWrite_Mem(RegWrite_Mem), .Rd_Ex(Rd_Ex), .RegWrite_Ex(RegWrite_Ex), .Inst_Rx(Inst_Ra),
    .Rd_Mem(Rd_Mem), .MEM_HAZARD(mem_sense_1_mem_hazard));
  WB_SENSE wb_sense_1 (
    .RegWrite_Wb(RegWrite_Wb), .RegWrite_Mem(RegWrite_Mem), .Rd_Ex(Rd_Ex), .RegWrite_Ex(RegWrite_Ex),
    .Rd_Mem(Rd_Mem), .Inst_Rx(Inst_Ra), .Rd_Wb(Rd_Wb), .WB_HAZARD(wb_sense_1_wb_hazard));
  EX_SENSE ex_sense_2 (.Rd_Ex(Rd_Ex), .RegWrite_Ex(RegWrite_Ex), .Inst_Rx(Inst_Rb), .EX_HAZARD(ex_sense_2_ex_hazard));
  MEM_SENSE mem_sense_2 (
    .RegWrite_Mem(RegWrite_Mem), .Rd_Ex(Rd_Ex), .RegWrite_Ex(RegWrite_Ex), .Inst_Rx(Inst_Rb),
    .Rd_Mem(Rd_Mem), .MEM_HAZARD(mem_sense_2_mem_hazard));
  WB_SENSE wb_sense_2 (
    .RegWrite_Wb(RegWrite_Wb), .RegWrite_Mem(RegWrite_Mem), .Rd_Ex(Rd_Ex), .RegWrite_Ex(RegWrite_Ex),
    .Rd_Mem(Rd_Mem), .Inst_Rx(Inst_Rb), .Rd_Wb(Rd_Wb), .WB_HAZARD(wb_sense_2_wb_hazard));
  Priority_Encoder #(.select(2)) priority_encoder_1 (
    .in0(1'b1), .in1(ex_sense_1_ex_hazard), .in2(mem_sense_1_mem_hazard), .in3(wb_sense_1_wb_hazard),
    .out(ForwardA));  // open: gs, en_out, en_in
  Priority_Encoder #(.select(2)) priority_encoder_2 (
    .in0(1'b1), .in1(ex_sense_2_ex_hazard), .in2(mem_sense_2_mem_hazard), .in3(wb_sense_2_wb_hazard),
    .out(ForwardB));  // open: gs, en_out, en_in
endmodule

module EX_SENSE (
  input  [2:0] Rd_Ex,
  input  RegWrite_Ex,
  input  [2:0] Inst_Rx,
  output EX_HAZARD
);

  wire comparator_1_eq, comparator_1_lt, comparator_2_eq, not_1_out;

  Comparator #(.mode("unsigned"), .width(3)) comparator_1 (
    .a(Rd_Ex), .b(3'b000), .eq(comparator_1_eq), .lt(comparator_1_lt));  // open: gt
  Comparator #(.mode("unsigned"), .width(3)) comparator_2 (
    .a(Rd_Ex), .b(Inst_Rx), .eq(comparator_2_eq));  // open: gt, lt
  not not_1 (not_1_out, comparator_1_eq);
  and and_1 (EX_HAZARD, RegWrite_Ex, not_1_out, comparator_2_eq);
endmodule

module MEM_SENSE (
  input  RegWrite_Mem,
  input  [2:0] Rd_Ex,
  input  RegWrite_Ex,
  input  [2:0] Inst_Rx,
  input  [2:0] Rd_Mem,
  output MEM_HAZARD
);

  wire comparator_1_eq, comparator_2_eq, ex_sense_1_ex_hazard, not_1_out, not_2_out;

  EX_SENSE ex_sense_1 (.Rd_Ex(Rd_Ex), .RegWrite_Ex(RegWrite_Ex), .Inst_Rx(Inst_Rx), .EX_HAZARD(ex_sense_1_ex_hazard));
  not not_1 (not_1_out, ex_sense_1_ex_hazard);
  Comparator #(.width(3)) comparator_1 (.a(Rd_Mem), .b(3'b000), .eq(comparator_1_eq));  // open: gt, lt
  not not_2 (not_2_out, comparator_1_eq);
  Comparator #(.width(3)) comparator_2 (.a(Rd_Mem), .b(Inst_Rx), .eq(comparator_2_eq));  // open: gt, lt
  and and_1 (MEM_HAZARD, RegWrite_Mem, not_1_out, not_2_out, comparator_2_eq);
endmodule

module WB_SENSE (
  input  RegWrite_Wb,
  input  RegWrite_Mem,
  input  [2:0] Rd_Ex,
  input  RegWrite_Ex,
  input  [2:0] Rd_Mem,
  input  [2:0] Inst_Rx,
  input  [2:0] Rd_Wb,
  output WB_HAZARD
);

  wire comparator_1_eq, comparator_2_eq, ex_sense_1_ex_hazard, mem_sense_1_mem_hazard, not_1_out, not_2_out,
       not_3_out;

  MEM_SENSE mem_sense_1 (
    .RegWrite_Mem(RegWrite_Mem), .Rd_Ex(Rd_Ex), .RegWrite_Ex(RegWrite_Ex), .Inst_Rx(Inst_Rx),
    .Rd_Mem(Rd_Mem), .MEM_HAZARD(mem_sense_1_mem_hazard));
  EX_SENSE ex_sense_1 (.Rd_Ex(Rd_Ex), .RegWrite_Ex(RegWrite_Ex), .Inst_Rx(Inst_Rx), .EX_HAZARD(ex_sense_1_ex_hazard));
  not not_1 (not_1_out, mem_sense_1_mem_hazard);
  Comparator #(.width(3)) comparator_1 (.a(Rd_Wb), .b(Inst_Rx), .eq(comparator_1_eq));  // open: gt, lt
  Comparator #(.width(3)) comparator_2 (.a(Inst_Rx), .b(3'b000), .eq(comparator_2_eq));  // open: gt, lt
  not not_2 (not_2_out, ex_sense_1_ex_hazard);
  not not_3 (not_3_out, comparator_2_eq);
  and and_1 (WB_HAZARD, RegWrite_Wb, not_1_out, comparator_1_eq, not_3_out, not_2_out);
endmodule
