// Logisim project orReduceGate.circ as structural Verilog: 1 circuit, main circuit orReduce
module orReduce (
  input  [31:0] stringIn,
  output orReduce
);

  or or_1 (orReduce, stringIn[0], stringIn[1], stringIn[2], stringIn[3], stringIn[4], stringIn[5], stringIn[6], stringIn[7], stringIn[8], stringIn[9], stringIn[10], stringIn[11], stringIn[12], stringIn[13], stringIn[14], stringIn[15], stringIn[16], stringIn[17], stringIn[18], stringIn[19], stringIn[20], stringIn[21], stringIn[22], stringIn[23], stringIn[24], stringIn[25], stringIn[26], stringIn[27], stringIn[28], stringIn[29], stringIn[30], stringIn[31]);
endmodule
