// Logisim project pcControl.circ as structural Verilog: 1 circuit, main circuit PCBox
module PCBox (
  input  [19:0] PC,
  input  [10:0] Imm11,
  input  [4:0] Imm5,
  input  [31:0] regValue,
  input  applyImmediateExtension,
  input  [10:0] Extension_Imm11,
  input  applyBranch,
  input  jumpImmediate,
  input  jumpReg,
  output [19:0] nextPC,
  output Kill2,
  output Kill1
);

  wire [19:0] adder_1_out, adder_2_out, adder_3_out, adder_4_out, adder_5_out, bit_extender_1_out,
       bit_extender_2_out, bit_extender_3_out, multiplexer_1_out, multiplexer_2_out, multiplexer_3_out;

  assign bit_extender_1_out = {{15{Imm5[4]}}, Imm5};  // Bit_Extender bit_extender_1
  assign bit_extender_2_out = {{4{Extension_Imm11[10]}}, {Extension_Imm11, Imm5}};  // Bit_Extender bit_extender_2
  assign bit_extender_3_out = {{9{Imm11[10]}}, Imm11};  // Bit_Extender bit_extender_3
  Multiplexer #(.width(20)) multiplexer_1 (
    .in0(bit_extender_1_out), .in1(bit_extender_2_out), .out(multiplexer_1_out), .sel(applyImmediateExtension));
  Adder #(.width(20)) adder_1 (.a(20'h1), .b(PC), .out(adder_1_out));  // open: cin, cout
  Adder #(.width(20)) adder_2 (.a(PC), .b(bit_extender_3_out), .out(adder_2_out));  // open: cin, cout
  Adder #(.width(20)) adder_3 (.a(PC), .b(multiplexer_1_out), .out(adder_3_out));  // open: cin, cout
  Adder #(.width(20)) adder_4 (.a({20{1'b1}}), .b(adder_2_out), .out(adder_4_out));  // open: cin, cout
  Adder #(.width(20)) adder_5 (.a(20'hffffe), .b(adder_3_out), .out(adder_5_out));  // open: cin, cout
  Multiplexer #(.width(20)) multiplexer_2 (
    .in0(adder_1_out), .in1(regValue[19:0]), .out(multiplexer_2_out), .sel(jumpReg));
  Multiplexer #(.width(20)) multiplexer_3 (
    .in0(multiplexer_2_out), .in1(adder_4_out), .out(multiplexer_3_out), .sel(jumpImmediate));
  Multiplexer #(.width(20)) multiplexer_4 (.in0(multiplexer_3_out), .in1(adder_5_out), .out(nextPC), .sel(applyBranch));
  or or_1 (Kill1, jumpReg, applyBranch, jumpImmediate);

  assign Kill2 = applyBranch;
endmodule
