// Logisim project pipeLine.circ as structural Verilog: 1 circuit, main circuit DataPath
module DataPath (
);

  wire alu_1_lessthan, alu_1_zero, ALUSrc_Ex_q, applyImmediate, branchcontrol_1_applybranch, clock_1_out,
       clock_2_out, clock_3_out, clock_4_out, clock_5_out, clock_6_out, clock_7_out, clock_8_out,
       clock_9_out, clock_10_out, clock_11_out, clock_12_out, clock_13_out, clock_14_out, clock_15_out,
       clock_16_out, clock_17_out, clock_18_out, clock_19_out, clock_20_out, clock_21_out, clock_22_out,
       clock_23_out, clock_24_out, clock_25_out, clock_26_out, clock_27_out, clock_28_out, clock_29_out,
       clock_30_out, clock_31_out, clock_32_out, maincontrol_1_alusrc, maincontrol_1_eqbranch,
       maincontrol_1_forcer7, maincontrol_1_gebranch, maincontrol_1_jumpimm, maincontrol_1_jumpreg,
       maincontrol_1_ltbranch, maincontrol_1_memread, maincontrol_1_memwrite, maincontrol_1_noteqbranch,
       maincontrol_1_regdst, maincontrol_1_regwrite, maincontrol_1_writeaddress, MemRd_Mem_q, MemRead_Ex_q,
       MemWr_Ex_q, MemWr_Mem_q, multiplexer_2_out, multiplexer_3_out, multiplexer_4_out, multiplexer_5_out,
       multiplexer_9_out, multiplexer_10_out, not_1_out, pcbox_1_kill1, pcbox_1_kill2, register_5_q,
       register_6_q, register_7_q, register_8_q, RegWrite_Ex_q, RegWrite_Mem_q, RegWrite_Wb_q, Stall,
       stallcontrol_1_stall, undriven, writeAddress_Ex_q, writeAddress_Mem_q;
  wire [1:0] forwardcontrol_1_forwarda, forwardcontrol_1_forwardb, instructionsplitter_1_func;
  wire [2:0] instructionsplitter_1_rega, instructionsplitter_1_regb, instructionsplitter_1_regd,
       multiplexer_6_out, multiplexer_7_out, Rd_Ex_q, Rd_Mem_q, Rd_Wb_q;
  wire [3:0] alucontrol_1_aluselect, ALUSelect_Ex_q, maincontrol_1_aluop;
  wire [4:0] instructionsplitter_1_imm5, instructionsplitter_1_opcode, register_4_q;
  wire [10:0] ExtensionImm11, instructionsplitter_1_imm11;
  wire [15:0] multiplexer_1_out, register_3_q, rom_1_data;
  wire [19:0] adder_1_out, pcbox_1_nextpc, register_1_q, register_2_q, register_9_q, register_12_q;
  wire [31:0] alu_1_aluresult, bit_extender_1_out, bit_extender_2_out, bit_extender_3_out, Imm_Ex_q,
       multiplexer_8_out, multiplexer_11_out, multiplexer_12_out, multiplexer_13_out, multiplexer_14_out,
       multiplexer_15_out, ram_1_dout, register_10_q, register_11_q, register_13_q, register_14_q,
       register_15_q, registerfile_1_readdata1, registerfile_1_readdata2, registerfile_1_reg1,
       registerfile_1_reg2, registerfile_1_reg3, registerfile_1_reg4, registerfile_1_reg5,
       registerfile_1_reg6, registerfile_1_reg7;

  not not_1 (not_1_out, stallcontrol_1_stall);
  Register #(.width(20)) register_1 (
    .D(pcbox_1_nextpc), .en(not_1_out), .clk(clock_1_out), .Q(register_1_q), .clr(undriven));
  Clock clock_1 (.out(clock_1_out));
  ROM #(.addrWidth(20), .dataWidth(16)) rom_1 (.addr(register_1_q), .data(rom_1_data));
  Adder #(.width(20)) adder_1 (.a(20'h1), .b(register_1_q), .out(adder_1_out));  // open: cin, cout
  Register #(.width(20)) register_2 (.D(adder_1_out), .en(1'b1), .clk(clock_2_out), .Q(register_2_q));  // open: clr
  Clock clock_2 (.out(clock_2_out));
  Multiplexer #(.width(16)) multiplexer_1 (
    .in0(rom_1_data), .in1({16{1'b0}}), .out(multiplexer_1_out), .sel(pcbox_1_kill1));
  Register #(.width(16)) register_3 (
    .D(multiplexer_1_out), .en(not_1_out), .clk(clock_3_out), .Q(register_3_q));  // open: clr
  Clock clock_3 (.out(clock_3_out));
  Register #(.width(5)) register_4 (
    .D(instructionsplitter_1_imm5), .en(1'b1), .clk(clock_4_out), .Q(register_4_q));  // open: clr
  Clock clock_4 (.out(clock_4_out));
  instructionSplitter instructionsplitter_1 (
    .instruction(register_3_q), .func(instructionsplitter_1_func), .RegD(instructionsplitter_1_regd),
    .Imm5(instructionsplitter_1_imm5), .RegB(instructionsplitter_1_regb), .RegA(instructionsplitter_1_rega),
    .Imm11(instructionsplitter_1_imm11), .Opcode(instructionsplitter_1_opcode));
  Multiplexer multiplexer_2 (.in0(maincontrol_1_eqbranch), .in1(1'b0), .out(multiplexer_2_out), .sel(Stall));
  Multiplexer multiplexer_3 (.in0(maincontrol_1_gebranch), .in1(1'b0), .out(multiplexer_3_out), .sel(Stall));
  Multiplexer multiplexer_4 (.in0(maincontrol_1_noteqbranch), .in1(1'b0), .out(multiplexer_4_out), .sel(Stall));
  Multiplexer multiplexer_5 (.in0(maincontrol_1_ltbranch), .in1(1'b0), .out(multiplexer_5_out), .sel(Stall));
  MainControl maincontrol_1 (
    .OpCode(instructionsplitter_1_opcode), .EqBranch(maincontrol_1_eqbranch),
    .GeBranch(maincontrol_1_gebranch), .NotEqBranch(maincontrol_1_noteqbranch),
    .LtBranch(maincontrol_1_ltbranch), .RegDst(maincontrol_1_regdst), .ForceR7(maincontrol_1_forcer7),
    .MemRead(maincontrol_1_memread), .WriteAddress(maincontrol_1_writeaddress),
    .MemWrite(maincontrol_1_memwrite), .ALUSrc(maincontrol_1_alusrc), .RegWrite(maincontrol_1_regwrite),
    .JumpImm(maincontrol_1_jumpimm), .JumpReg(maincontrol_1_jumpreg), .ALUOp(maincontrol_1_aluop));  // open: WriteBus
  ImmLogic immlogic_1 (
    .OpCode(instructionsplitter_1_opcode), .nextInstruction(rom_1_data), .ApplyImm(applyImmediate),
    .Imm11(ExtensionImm11));
  Register #(.width(1)) register_5 (.D(multiplexer_2_out), .clk(clock_5_out), .Q(register_5_q));  // open: en, clr
  Clock clock_5 (.out(clock_5_out));
  Register #(.width(1)) register_6 (
    .D(multiplexer_3_out), .en(1'b1), .clk(clock_6_out), .Q(register_6_q));  // open: clr
  Clock clock_6 (.out(clock_6_out));
  Register #(.width(1)) register_7 (
    .D(multiplexer_4_out), .en(1'b1), .clk(clock_7_out), .Q(register_7_q));  // open: clr
  Clock clock_7 (.out(clock_7_out));
  stallControl stallcontrol_1 (
    .MemRd_Ex(MemRead_Ex_q), .ForwardA(forwardcontrol_1_forwarda), .ForwardB(forwardcontrol_1_forwardb),
    .Stall(stallcontrol_1_stall));
  Register #(.width(1)) register_8 (
    .D(multiplexer_5_out), .en(1'b1), .clk(clock_8_out), .Q(register_8_q));  // open: clr
  Clock clock_8 (.out(clock_8_out));
  Multiplexer #(.width(3)) multiplexer_6 (
    .in0(instructionsplitter_1_regd), .in1(instructionsplitter_1_regb), .out(multiplexer_6_out),
    .sel(maincontrol_1_regdst));
  or or_1 (Stall, stallcontrol_1_stall, pcbox_1_kill2);
  Multiplexer #(.width(3)) multiplexer_7 (
    .in0(multiplexer_6_out), .in1(3'b111), .out(multiplexer_7_out), .sel(maincontrol_1_forcer7));
  ALUControl alucontrol_1 (
    .ALUOp(maincontrol_1_aluop), .FuncCode(instructionsplitter_1_func), .ALUSelect(alucontrol_1_aluselect));
  Clock clock_9 (.out(clock_9_out));
  // Probe on registerfile_1_reg1
  assign bit_extender_1_out = {{27{instructionsplitter_1_imm5[4]}}, instructionsplitter_1_imm5};  // Bit_Extender bit_extender_1
  assign bit_extender_2_out = {{16{ExtensionImm11[10]}}, {ExtensionImm11, instructionsplitter_1_imm5}};  // Bit_Extender bit_extender_2
  // Probe on registerfile_1_reg2
  Register #(.width(1)) MemRead_Ex (
    .D(maincontrol_1_memread), .en(1'b1), .clk(clock_10_out), .Q(MemRead_Ex_q));  // open: clr
  Clock clock_10 (.out(clock_10_out));
  registerFile registerfile_1 (
    .WriteEnable(RegWrite_Wb_q), .WriteData(register_15_q), .WriteRegister(Rd_Wb_q), .clk(clock_9_out),
    .readReg2(instructionsplitter_1_regb), .readReg1(instructionsplitter_1_rega),
    .readData2(registerfile_1_readdata2), .readData1(registerfile_1_readdata1), .reg2(registerfile_1_reg2),
    .reg3(registerfile_1_reg3), .reg4(registerfile_1_reg4), .reg7(registerfile_1_reg7),
    .reg5(registerfile_1_reg5), .reg6(registerfile_1_reg6), .reg1(registerfile_1_reg1));
  Multiplexer #(.width(32)) multiplexer_8 (
    .in0(bit_extender_1_out), .in1(bit_extender_2_out), .out(multiplexer_8_out), .sel(applyImmediate));
  Multiplexer multiplexer_9 (.in0(maincontrol_1_regwrite), .in1(1'b0), .out(multiplexer_9_out), .sel(Stall));
  // Probe on registerfile_1_reg3
  Register #(.width(32)) Imm_Ex (.D(multiplexer_8_out), .en(1'b1), .clk(clock_11_out), .Q(Imm_Ex_q));  // open: clr
  Clock clock_11 (.out(clock_11_out));
  Clock clock_12 (.out(clock_12_out));
  Clock clock_13 (.out(clock_13_out));
  forwardControl forwardcontrol_1 (
    .Rd_Ex(Rd_Ex_q), .RegWrite_Ex(RegWrite_Ex_q), .Inst_Ra(instructionsplitter_1_rega),
    .RegWrite_Mem(RegWrite_Mem_q), .Rd_Mem(Rd_Mem_q), .RegWrite_Wb(RegWrite_Wb_q), .Rd_Wb(Rd_Wb_q),
    .Inst_Rb(instructionsplitter_1_regb), .ForwardA(forwardcontrol_1_forwarda),
    .ForwardB(forwardcontrol_1_forwardb));
  Register #(.width(1)) MemWr_Ex (.D(multiplexer_10_out), .en(1'b1), .clk(clock_14_out), .Q(MemWr_Ex_q));  // open: clr
  Multiplexer multiplexer_10 (.in0(maincontrol_1_memwrite), .in1(1'b0), .out(multiplexer_10_out), .sel(Stall));
  Clock clock_14 (.out(clock_14_out));
  Register #(.width(1)) ALUSrc_Ex (
    .D(maincontrol_1_alusrc), .en(1'b1), .clk(clock_15_out), .Q(ALUSrc_Ex_q));  // open: clr
  Clock clock_15 (.out(clock_15_out));
  Register #(.width(4)) ALUSelect_Ex (
    .D(alucontrol_1_aluselect), .en(1'b1), .clk(clock_16_out), .Q(ALUSelect_Ex_q));  // open: clr
  Clock clock_16 (.out(clock_16_out));
  Register #(.width(3)) Rd_Ex (.D(multiplexer_7_out), .en(1'b1), .clk(clock_17_out), .Q(Rd_Ex_q));  // open: clr
  Clock clock_17 (.out(clock_17_out));
  Register #(.width(1)) RegWrite_Ex (
    .D(multiplexer_9_out), .en(1'b1), .clk(clock_12_out), .Q(RegWrite_Ex_q));  // open: clr
  Register #(.width(20)) register_9 (.D(register_2_q), .en(1'b1), .clk(clock_13_out), .Q(register_9_q));  // open: clr
  // Probe on registerfile_1_reg4
  Register #(.width(1)) writeAddress_Ex (
    .D(maincontrol_1_writeaddress), .en(1'b1), .clk(clock_18_out), .Q(writeAddress_Ex_q));  // open: clr
  Clock clock_18 (.out(clock_18_out));
  Register #(.width(32)) register_10 (
    .D(multiplexer_11_out), .en(1'b1), .clk(clock_19_out), .Q(register_10_q));  // open: clr
  Multiplexer #(.select(2), .width(32)) multiplexer_11 (
    .in0(registerfile_1_readdata1), .in1(alu_1_aluresult), .in2(multiplexer_15_out), .in3(register_15_q),
    .out(multiplexer_11_out), .sel(forwardcontrol_1_forwarda));
  Clock clock_19 (.out(clock_19_out));
  Register #(.width(32)) register_11 (
    .D(multiplexer_12_out), .en(1'b1), .clk(clock_20_out), .Q(register_11_q));  // open: clr
  Multiplexer #(.select(2), .width(32)) multiplexer_12 (
    .in0(registerfile_1_readdata2), .in1(alu_1_aluresult), .in2(multiplexer_15_out), .in3(register_15_q),
    .out(multiplexer_12_out), .sel(forwardcontrol_1_forwardb));
  Clock clock_20 (.out(clock_20_out));
  // Probe on registerfile_1_reg5
  branchControl branchcontrol_1 (
    .geBranch(register_6_q), .lessThan(alu_1_lessthan), .zero(alu_1_zero), .LtBranch(register_8_q),
    .notEqBranch(register_7_q), .EqBranch(register_5_q), .applyBranch(branchcontrol_1_applybranch));
  Multiplexer #(.width(32)) multiplexer_13 (
    .in0(register_11_q), .in1(Imm_Ex_q), .out(multiplexer_13_out), .sel(ALUSrc_Ex_q));
  // Probe on registerfile_1_reg6
  ALU alu_1 (
    .input1(register_10_q), .input2(multiplexer_13_out), .ALUControl(ALUSelect_Ex_q),
    .ALUResult(alu_1_aluresult), .Zero(alu_1_zero), .LessThan(alu_1_lessthan));
  // Probe on registerfile_1_reg7
  Register #(.width(1)) writeAddress_Mem (
    .D(writeAddress_Ex_q), .en(1'b1), .clk(clock_21_out), .Q(writeAddress_Mem_q));  // open: clr
  Clock clock_21 (.out(clock_21_out));
  PCBox pcbox_1 (
    .PC(register_1_q), .Imm11(instructionsplitter_1_imm11), .Imm5(register_4_q),
    .regValue(registerfile_1_readdata1), .applyImmediateExtension(applyImmediate),
    .Extension_Imm11(ExtensionImm11), .applyBranch(branchcontrol_1_applybranch),
    .jumpImmediate(maincontrol_1_jumpimm), .jumpReg(maincontrol_1_jumpreg), .nextPC(pcbox_1_nextpc),
    .Kill2(pcbox_1_kill2), .Kill1(pcbox_1_kill1));
  Register #(.width(1)) MemWr_Mem (.D(MemWr_Ex_q), .en(1'b1), .clk(clock_22_out), .Q(MemWr_Mem_q));  // open: clr
  Clock clock_22 (.out(clock_22_out));
  Register #(.width(20)) register_12 (.D(register_9_q), .en(1'b1), .clk(clock_23_out), .Q(register_12_q));  // open: clr
  Clock clock_23 (.out(clock_23_out));
  Register #(.width(1)) MemRd_Mem (.D(MemRead_Ex_q), .en(1'b1), .clk(clock_24_out), .Q(MemRd_Mem_q));  // open: clr
  Clock clock_24 (.out(clock_24_out));
  Register #(.width(32)) register_13 (
    .D(alu_1_aluresult), .en(1'b1), .clk(clock_25_out), .Q(register_13_q));  // open: clr
  Clock clock_25 (.out(clock_25_out));
  Register #(.width(32)) register_14 (
    .D(register_11_q), .en(1'b1), .clk(clock_26_out), .Q(register_14_q));  // open: clr
  Clock clock_26 (.out(clock_26_out));
  Register #(.width(3)) Rd_Mem (.D(Rd_Ex_q), .en(1'b1), .clk(clock_27_out), .Q(Rd_Mem_q));  // open: clr
  Clock clock_27 (.out(clock_27_out));
  Register #(.width(1)) RegWrite_Mem (
    .D(RegWrite_Ex_q), .en(1'b1), .clk(clock_28_out), .Q(RegWrite_Mem_q));  // open: clr
  Clock clock_28 (.out(clock_28_out));
  RAM #(.addrWidth(20), .dataWidth(32), .enables("line")) ram_1 (
    .addr(register_13_q[19:0]), .we(MemWr_Mem_q), .clk(clock_29_out), .din(register_14_q), .dout(ram_1_dout));
  Clock clock_29 (.out(clock_29_out));
  Multiplexer #(.width(32)) multiplexer_14 (
    .in0(register_13_q), .in1(ram_1_dout), .out(multiplexer_14_out), .sel(MemRd_Mem_q));
  assign bit_extender_3_out = {{12{register_12_q[19]}}, register_12_q};  // Bit_Extender bit_extender_3
  Multiplexer #(.width(32)) multiplexer_15 (
    .in0(multiplexer_14_out), .in1(bit_extender_3_out), .out(multiplexer_15_out), .sel(writeAddress_Mem_q));
  Register #(.width(32)) register_15 (
    .D(multiplexer_15_out), .en(1'b1), .clk(clock_30_out), .Q(register_15_q));  // open: clr
  Clock clock_30 (.out(clock_30_out));
  Register #(.width(3)) Rd_Wb (.D(Rd_Mem_q), .en(1'b1), .clk(clock_31_out), .Q(Rd_Wb_q));  // open: clr
  Clock clock_31 (.out(clock_31_out));
  Register #(.width(1)) RegWrite_Wb (
    .D(RegWrite_Mem_q), .en(1'b1), .clk(clock_32_out), .Q(RegWrite_Wb_q));  // open: clr
  Clock clock_32 (.out(clock_32_out));

  // Notes on the sheet:
  //   contents of rom_1 (hex, n*v repeats v):
  //   3044 407e 389e 934 a39 95f 59e4 394 156 177 64a4 69a4 71a4 7ba4 934 cb9 5dc 35af a820 a884 a0a0 a820
  //   a884 a0a0 a0c4 26eb a8e8 a0a0 a8ac 8122 a54 8823 a58 c9c e004 a54 c98 0 3025 e804 216 8000 0 3041
  //   3061 a6c a69 413f 891d df00 a49
  //   R1
  //   R2
  //   R3
  //   R4
  //   R5
  //   R6
  //   R7
endmodule
