// Logisim project stallCircuit.circ as structural Verilog: 1 circuit, main circuit stallControl
module stallControl (
  input  MemRd_Ex,
  input  [1:0] ForwardA,
  input  [1:0] ForwardB,
  output Stall
);

  wire comparator_1_eq, comparator_2_eq, or_1_out;

  Comparator #(.width(2)) comparator_1 (.a(2'b01), .b(ForwardA), .eq(comparator_1_eq));  // open: gt, lt
  Comparator #(.width(2)) comparator_2 (.a(2'b01), .b(ForwardB), .eq(comparator_2_eq));  // open: gt, lt
  or or_1 (or_1_out, comparator_1_eq, comparator_2_eq);
  and and_1 (Stall, MemRd_Ex, or_1_out);
endmodule
